# Fritzing sketch MazeGame_wArduino_Uno (saved by Fritzing 0.8.3b)
circuit board: 22.2202cm x 10.7695cm
breadboards: 2

parts:
  Part1 = Arduino Uno (Rev3)
  U1 = 74HC595 [package="DIP16 [THT]"]
  U2 = 74HC595 [package="DIP16 [THT]"]
  Part3 = Triple Axis Accelerometer Breakout - ADXL335
  R1 = Resistor [tolerance=±5% resistance=220 package=THT]
  R2 = Resistor [tolerance=±5% resistance=220 package=THT]
  R3 = Resistor [tolerance=±5% resistance=220 package=THT]
  R4 = Resistor [tolerance=±5% resistance=220 package=THT]
  R5 = Resistor [tolerance=±5% resistance=220 package=THT]
  R6 = Resistor [tolerance=±5% resistance=220 package=THT]
  R7 = Resistor [tolerance=±5% resistance=220 package=THT]
  R8 = Resistor [tolerance=±5% resistance=220 package=THT]
  8x8_LED_Matrix1 = 8x8 LED Matrix 1588ASR

nets:
  N1: Part1.A1, Part3.XOUT
  N2: Part1.A3, Part3.YOUT
  N3: Part1.A5/SCL, Part3.ZOUT
  GND: Part1.GND, U1.GND, U1.OE, U2.GND, U2.OE, Part3.GND
  N4: Part1.D3_PWM, U1.DS
  N5: Part1.D5_PWM, U1.ST_CP, U2.ST_CP
  VCC: Part1.5V, U1.MR, U1.VCC, U2.MR, U2.VCC
  N6: U1.Q1, R7.Pin_0, R7.Pin_1, 8x8_LED_Matrix1.Pin_1
  N7: U1.Q2, R3.Pin_0, R3.Pin_1, 8x8_LED_Matrix1.Pin_2
  N8: U1.Q3, 8x8_LED_Matrix1.Pin_3
  N9: U1.Q4, 8x8_LED_Matrix1.Pin_4
  N10: U1.Q5, 8x8_LED_Matrix1.Pin_15
  N11: U1.Q6, R1.Pin_0, R1.Pin_1, 8x8_LED_Matrix1.Pin14
  N12: U1.Q7, 8x8_LED_Matrix1.Pin_13
  N13: U1.Q7', U2.DS
  N14: U1.SH_CP, U2.SH_CP
  N15: U1.Q0, 8x8_LED_Matrix1.Pin_16
  N16: U2.Q1, R8.Pin_0, R8.Pin_1, 8x8_LED_Matrix1.Pin_8
  N17: U2.Q2, 8x8_LED_Matrix1.Pin_7
  N18: U2.Q3, R6.Pin_0, R6.Pin_1, 8x8_LED_Matrix1.Pin_6
  N19: U2.Q4, R5.Pin_0, R5.Pin_1, 8x8_LED_Matrix1.Pin_5
  N20: U2.Q5, R2.Pin_0, R2.Pin_1, 8x8_LED_Matrix1.Pin_12
  N21: U2.Q6, 8x8_LED_Matrix1.Pin_11
  N22: U2.Q7, 8x8_LED_Matrix1.Pin_10
  N23: U2.Q0, R4.Pin_0, R4.Pin_1, 8x8_LED_Matrix1.Pin_9

notes:
  3.3V to the Accelerometer
  5V to the Shift Registers
  I kept the accelerometer and 8x8 on the same board, but they could be separated
  The 2 shift registers are chained together to reduce pin usage on the uController
  I ran wire out from under the 8x8 rather than straddling two boards

custom parts:
  8x8 LED Matrix 1588ASR: Red Color Common cathode 8x8 LED Matrix
